# Fritzing sketch multiprise (saved by Fritzing 0.9.3b)
breadboards: 1

parts:
  U1 = NodeMCU V3.0
  U2 = 8RelayModule
  ZS-042_RTC1 = ZS-042 RTC Module

nets:
  N1: U1.D1, ZS-042_RTC1.SCL
  N2: U1.D2, ZS-042_RTC1.SDA
  N3: U1.D3, U2.IN3
  N4: U1.D4, U2.IN5
  N5: U1.GND#6, U1.GND#13, U1.GND#16, U1.GND#33, ZS-042_RTC1.GND
  N6: U1.D5, U2.IN6
  N7: U1.D6, U2.IN7
  N8: U1.D7, U2.IN8
  N9: U1.D8, U2.IN4
  N10: U1.VU, U2.VCC#11, ZS-042_RTC1.VCC
  N11: U1.GND#41, U2.GND
  N12: U2.JD-VCC, U2.VCC#12

custom parts:
  NodeMCU V3.0: ESP8266 based NodeMCU
  8RelayModule: 8 relay arduino module SONGLE SRD05VDC-SL-C
